// Logisim project BasicGates.circ as structural Verilog: 1 circuit, main circuit main
module main (
  input  in_1,
  input  in_2,
  input  in_3,
  input  in_4,
  input  in_5,
  output out_6,
  output out_7,
  output out_8
);

  not \not  (out_6, in_1);
  and \and  (out_7, in_2, in_3);
  or \or  (out_8, in_4, in_5);
endmodule
