// Logisim project DontPanic.circ as structural Verilog: 1 circuit, main circuit main
module main (
  input  in_1,
  output DON_T_LED1,
  output DON_T_LED2,
  output PANIC_LED3,
  output PANIC_LED1,
  output PANIC_LED4,
  output PANIC_LED2
);

  // _7404 7404_1: pin names not known; wires that end beside it: in_1, DON_T_LED1, 1'b0, 1'b1

  assign DON_T_LED2 = DON_T_LED1;
  assign PANIC_LED1 = 1'b1;
  assign PANIC_LED2 = 1'b1;
  assign PANIC_LED3 = in_1;
  assign PANIC_LED4 = in_1;

  // Notes on the sheet:
  //   PANIC
  //   DON'T
endmodule
