// Logisim project DontPanic2.circ as structural Verilog: 2 circuits, main circuit main
module main (
);

  wire clock_1_out, demultiplexer_1_out0, demultiplexer_1_out1, demultiplexer_1_out2, demultiplexer_1_out3,
       demultiplexer_1_out4, demultiplexer_1_out5, demultiplexer_1_out6, demultiplexer_1_out7;
  wire [2:0] counter_1_q;
  wire [7:0] ram_1_data;

  Clock clock_1 (.out(clock_1_out));
  Counter #(.width(3), .max('h7)) counter_1 (.Q(counter_1_q), .clk(clock_1_out));  // open: load, D, count, carry, clr
  RAM #(.addrWidth(3), .bus("asynch")) ram_1 (.addr(counter_1_q), .data(ram_1_data));  // open: sel, ld, clr
  _8x8_LED_Matrix u_8x8_led_matrix_1 (
    .in_1(ram_1_data[7]), .in_2(ram_1_data[6]), .in_3(ram_1_data[5]), .in_4(ram_1_data[4]),
    .in_5(ram_1_data[3]), .in_6(ram_1_data[2]), .in_7(ram_1_data[1]), .in_8(ram_1_data[0]),
    .in_9(demultiplexer_1_out0), .in_10(demultiplexer_1_out1), .in_11(demultiplexer_1_out2),
    .in_12(demultiplexer_1_out3), .in_13(demultiplexer_1_out4), .in_14(demultiplexer_1_out5),
    .in_15(demultiplexer_1_out6), .in_16(demultiplexer_1_out7));
  Demultiplexer #(.select(3)) demultiplexer_1 (
    .out0(demultiplexer_1_out0), .out1(demultiplexer_1_out1), .out2(demultiplexer_1_out2),
    .out3(demultiplexer_1_out3), .out4(demultiplexer_1_out4), .out5(demultiplexer_1_out5),
    .out6(demultiplexer_1_out6), .out7(demultiplexer_1_out7), .in(1'b1), .sel(counter_1_q));  // open: en
endmodule

module _8x8_LED_Matrix (
  input  in_1,
  input  in_2,
  input  in_3,
  input  in_4,
  input  in_5,
  input  in_6,
  input  in_7,
  input  in_8,
  input  in_9,
  input  in_10,
  input  in_11,
  input  in_12,
  input  in_13,
  input  in_14,
  input  in_15,
  input  in_16
);

  wire and_1_out, and_2_out, and_3_out, and_4_out, and_5_out, and_6_out, and_7_out, and_8_out, and_9_out,
       and_10_out, and_11_out, and_12_out, and_13_out, and_14_out, and_15_out, and_16_out, and_17_out,
       and_18_out, and_19_out, and_20_out, and_21_out, and_22_out, and_23_out, and_24_out, and_25_out,
       and_26_out, and_27_out, and_28_out, and_29_out, and_30_out, and_31_out, and_32_out, and_33_out,
       and_34_out, and_35_out, and_36_out, and_37_out, and_38_out, and_39_out, and_40_out, and_41_out,
       and_42_out, and_43_out, and_44_out, and_45_out, and_46_out, and_47_out, and_48_out, and_49_out,
       and_50_out, and_51_out, and_52_out, and_53_out, and_54_out, and_55_out, and_56_out, and_57_out,
       and_58_out, and_59_out, and_60_out, and_61_out, and_62_out, and_63_out, and_64_out;

  and and_1 (and_1_out, in_1, in_9);
  and and_2 (and_2_out, in_2, in_9);
  LED led_1 (.in(and_1_out));
  LED led_2 (.in(and_2_out));
  LED led_3 (.in(and_4_out));
  LED led_4 (.in(and_3_out));
  and and_3 (and_3_out, in_1, in_10);
  and and_4 (and_4_out, in_2, in_10);
  and and_5 (and_5_out, in_1, in_11);
  LED led_5 (.in(and_6_out));
  LED led_6 (.in(and_5_out));
  and and_6 (and_6_out, in_2, in_11);
  and and_7 (and_7_out, in_2, in_12);
  LED led_7 (.in(and_7_out));
  and and_8 (and_8_out, in_1, in_12);
  LED led_8 (.in(and_8_out));
  LED led_9 (.in(and_10_out));
  LED led_10 (.in(and_9_out));
  and and_9 (and_9_out, in_2, in_13);
  and and_10 (and_10_out, in_1, in_13);
  LED led_11 (.in(and_12_out));
  and and_11 (and_11_out, in_2, in_14);
  LED led_12 (.in(and_11_out));
  and and_12 (and_12_out, in_1, in_14);
  LED led_13 (.in(and_14_out));
  LED led_14 (.in(and_13_out));
  and and_13 (and_13_out, in_1, in_15);
  and and_14 (and_14_out, in_2, in_15);
  and and_15 (and_15_out, in_1, in_16);
  LED led_15 (.in(and_15_out));
  and and_16 (and_16_out, in_2, in_16);
  LED led_16 (.in(and_16_out));
  and and_17 (and_17_out, in_3, in_9);
  LED led_17 (.in(and_17_out));
  LED led_18 (.in(and_18_out));
  and and_18 (and_18_out, in_3, in_10);
  LED led_19 (.in(and_19_out));
  and and_19 (and_19_out, in_3, in_11);
  and and_20 (and_20_out, in_3, in_12);
  LED led_20 (.in(and_20_out));
  LED led_21 (.in(and_21_out));
  and and_21 (and_21_out, in_3, in_13);
  and and_22 (and_22_out, in_3, in_14);
  LED led_22 (.in(and_22_out));
  LED led_23 (.in(and_23_out));
  and and_23 (and_23_out, in_3, in_15);
  LED led_24 (.in(and_24_out));
  and and_24 (and_24_out, in_3, in_16);
  LED led_25 (.in(and_25_out));
  and and_25 (and_25_out, in_4, in_9);
  LED led_26 (.in(and_26_out));
  and and_26 (and_26_out, in_4, in_10);
  and and_27 (and_27_out, in_4, in_11);
  LED led_27 (.in(and_27_out));
  LED led_28 (.in(and_28_out));
  and and_28 (and_28_out, in_4, in_12);
  and and_29 (and_29_out, in_4, in_13);
  LED led_29 (.in(and_29_out));
  LED led_30 (.in(and_30_out));
  and and_30 (and_30_out, in_4, in_14);
  and and_31 (and_31_out, in_4, in_15);
  LED led_31 (.in(and_31_out));
  and and_32 (and_32_out, in_4, in_16);
  LED led_32 (.in(and_32_out));
  LED led_33 (.in(and_33_out));
  and and_33 (and_33_out, in_5, in_9);
  and and_34 (and_34_out, in_5, in_10);
  LED led_34 (.in(and_34_out));
  and and_35 (and_35_out, in_5, in_11);
  LED led_35 (.in(and_35_out));
  and and_36 (and_36_out, in_5, in_12);
  LED led_36 (.in(and_36_out));
  and and_37 (and_37_out, in_5, in_13);
  LED led_37 (.in(and_37_out));
  LED led_38 (.in(and_38_out));
  and and_38 (and_38_out, in_5, in_14);
  LED led_39 (.in(and_39_out));
  and and_39 (and_39_out, in_5, in_15);
  LED led_40 (.in(and_40_out));
  and and_40 (and_40_out, in_5, in_16);
  and and_41 (and_41_out, in_6, in_9);
  LED led_41 (.in(and_41_out));
  and and_42 (and_42_out, in_6, in_10);
  LED led_42 (.in(and_42_out));
  LED led_43 (.in(and_43_out));
  and and_43 (and_43_out, in_6, in_11);
  LED led_44 (.in(and_44_out));
  and and_44 (and_44_out, in_6, in_12);
  and and_45 (and_45_out, in_6, in_13);
  LED led_45 (.in(and_45_out));
  and and_46 (and_46_out, in_6, in_14);
  LED led_46 (.in(and_46_out));
  and and_47 (and_47_out, in_6, in_15);
  LED led_47 (.in(and_47_out));
  LED led_48 (.in(and_48_out));
  and and_48 (and_48_out, in_6, in_16);
  and and_49 (and_49_out, in_7, in_9);
  LED led_49 (.in(and_49_out));
  and and_50 (and_50_out, in_7, in_10);
  LED led_50 (.in(and_50_out));
  LED led_51 (.in(and_51_out));
  and and_51 (and_51_out, in_7, in_11);
  and and_52 (and_52_out, in_7, in_12);
  LED led_52 (.in(and_52_out));
  and and_53 (and_53_out, in_7, in_13);
  LED led_53 (.in(and_53_out));
  and and_54 (and_54_out, in_7, in_14);
  LED led_54 (.in(and_54_out));
  LED led_55 (.in(and_55_out));
  and and_55 (and_55_out, in_7, in_15);
  LED led_56 (.in(and_56_out));
  and and_56 (and_56_out, in_7, in_16);
  LED led_57 (.in(and_57_out));
  and and_57 (and_57_out, in_8, in_9);
  LED led_58 (.in(and_58_out));
  and and_58 (and_58_out, in_8, in_10);
  and and_59 (and_59_out, in_8, in_11);
  LED led_59 (.in(and_59_out));
  and and_60 (and_60_out, in_8, in_12);
  LED led_60 (.in(and_60_out));
  LED led_61 (.in(and_61_out));
  and and_61 (and_61_out, in_8, in_13);
  LED led_62 (.in(and_62_out));
  and and_62 (and_62_out, in_8, in_14);
  LED led_63 (.in(and_63_out));
  and and_63 (and_63_out, in_8, in_15);
  LED led_64 (.in(and_64_out));
  and and_64 (and_64_out, in_8, in_16);
endmodule
