// Logisim project DontPanic3.circ as structural Verilog: 3 circuits, main circuit alternate
module _8x8_LED_Matrix (
  input  in_1,
  input  in_2,
  input  in_3,
  input  in_4,
  input  in_5,
  input  in_6,
  input  in_7,
  input  Sink__0_enables,
  input  in_9,
  input  in_10,
  input  in_11,
  input  in_12,
  input  in_13,
  input  in_14,
  input  in_15,
  input  in_16
);

  wire and_1_out, and_2_out, and_3_out, and_4_out, and_5_out, and_6_out, and_7_out, and_8_out, and_9_out,
       and_10_out, and_11_out, and_12_out, and_13_out, and_14_out, and_15_out, and_16_out, and_17_out,
       and_18_out, and_19_out, and_20_out, and_21_out, and_22_out, and_23_out, and_24_out, and_25_out,
       and_26_out, and_27_out, and_28_out, and_29_out, and_30_out, and_31_out, and_32_out, and_33_out,
       and_34_out, and_35_out, and_36_out, and_37_out, and_38_out, and_39_out, and_40_out, and_41_out,
       and_42_out, and_43_out, and_44_out, and_45_out, and_46_out, and_47_out, and_48_out, and_49_out,
       and_50_out, and_51_out, and_52_out, and_53_out, and_54_out, and_55_out, and_56_out, and_57_out,
       and_58_out, and_59_out, and_60_out, and_61_out, and_62_out, and_63_out, and_64_out, not_1_out,
       not_2_out, not_3_out, not_4_out, not_5_out, not_6_out, not_7_out, not_8_out;

  not not_1 (not_1_out, in_1);
  not not_2 (not_2_out, in_2);
  LED led_1 (.in(and_2_out));
  LED led_2 (.in(and_1_out));
  and and_1 (and_1_out, not_1_out, in_9);
  and and_2 (and_2_out, not_2_out, in_9);
  and and_3 (and_3_out, not_1_out, in_10);
  and and_4 (and_4_out, not_2_out, in_10);
  LED led_3 (.in(and_3_out));
  LED led_4 (.in(and_4_out));
  LED led_5 (.in(and_5_out));
  and and_5 (and_5_out, not_1_out, in_11);
  LED led_6 (.in(and_6_out));
  and and_6 (and_6_out, not_2_out, in_11);
  and and_7 (and_7_out, not_1_out, in_12);
  LED led_7 (.in(and_7_out));
  LED led_8 (.in(and_8_out));
  and and_8 (and_8_out, not_2_out, in_12);
  and and_9 (and_9_out, not_1_out, in_13);
  LED led_9 (.in(and_9_out));
  LED led_10 (.in(and_10_out));
  and and_10 (and_10_out, not_2_out, in_13);
  and and_11 (and_11_out, not_1_out, in_14);
  LED led_11 (.in(and_12_out));
  LED led_12 (.in(and_11_out));
  and and_12 (and_12_out, not_2_out, in_14);
  LED led_13 (.in(and_13_out));
  LED led_14 (.in(and_14_out));
  and and_13 (and_13_out, not_2_out, in_15);
  and and_14 (and_14_out, not_1_out, in_15);
  and and_15 (and_15_out, not_2_out, in_16);
  and and_16 (and_16_out, not_1_out, in_16);
  LED led_15 (.in(and_16_out));
  LED led_16 (.in(and_15_out));
  not not_3 (not_3_out, in_3);
  and and_17 (and_17_out, not_3_out, in_9);
  LED led_17 (.in(and_17_out));
  and and_18 (and_18_out, not_3_out, in_10);
  LED led_18 (.in(and_18_out));
  and and_19 (and_19_out, not_3_out, in_11);
  LED led_19 (.in(and_19_out));
  and and_20 (and_20_out, not_3_out, in_12);
  LED led_20 (.in(and_20_out));
  and and_21 (and_21_out, not_3_out, in_13);
  LED led_21 (.in(and_21_out));
  LED led_22 (.in(and_22_out));
  and and_22 (and_22_out, not_3_out, in_14);
  and and_23 (and_23_out, not_3_out, in_15);
  LED led_23 (.in(and_23_out));
  LED led_24 (.in(and_24_out));
  and and_24 (and_24_out, not_3_out, in_16);
  not not_4 (not_4_out, in_4);
  and and_25 (and_25_out, not_4_out, in_9);
  LED led_25 (.in(and_25_out));
  and and_26 (and_26_out, not_4_out, in_10);
  LED led_26 (.in(and_26_out));
  and and_27 (and_27_out, not_4_out, in_11);
  LED led_27 (.in(and_27_out));
  and and_28 (and_28_out, not_4_out, in_12);
  LED led_28 (.in(and_28_out));
  LED led_29 (.in(and_29_out));
  and and_29 (and_29_out, not_4_out, in_13);
  and and_30 (and_30_out, not_4_out, in_14);
  LED led_30 (.in(and_30_out));
  and and_31 (and_31_out, not_4_out, in_15);
  LED led_31 (.in(and_31_out));
  and and_32 (and_32_out, not_4_out, in_16);
  LED led_32 (.in(and_32_out));
  not not_5 (not_5_out, in_5);
  not not_6 (not_6_out, in_6);
  LED led_33 (.in(and_33_out));
  and and_33 (and_33_out, not_5_out, in_9);
  LED led_34 (.in(and_34_out));
  and and_34 (and_34_out, not_5_out, in_10);
  and and_35 (and_35_out, not_5_out, in_11);
  LED led_35 (.in(and_35_out));
  and and_36 (and_36_out, not_5_out, in_12);
  LED led_36 (.in(and_36_out));
  LED led_37 (.in(and_37_out));
  and and_37 (and_37_out, not_5_out, in_13);
  and and_38 (and_38_out, not_5_out, in_14);
  LED led_38 (.in(and_38_out));
  LED led_39 (.in(and_39_out));
  and and_39 (and_39_out, not_5_out, in_15);
  and and_40 (and_40_out, not_5_out, in_16);
  LED led_40 (.in(and_40_out));
  not not_7 (not_7_out, in_7);
  and and_41 (and_41_out, not_6_out, in_9);
  LED led_41 (.in(and_41_out));
  LED led_42 (.in(and_42_out));
  and and_42 (and_42_out, not_6_out, in_10);
  and and_43 (and_43_out, not_6_out, in_11);
  LED led_43 (.in(and_43_out));
  LED led_44 (.in(and_44_out));
  and and_44 (and_44_out, not_6_out, in_12);
  LED led_45 (.in(and_45_out));
  and and_45 (and_45_out, not_6_out, in_13);
  LED led_46 (.in(and_46_out));
  and and_46 (and_46_out, not_6_out, in_14);
  and and_47 (and_47_out, not_6_out, in_15);
  LED led_47 (.in(and_47_out));
  and and_48 (and_48_out, not_6_out, in_16);
  LED led_48 (.in(and_48_out));
  not not_8 (not_8_out, Sink__0_enables);
  LED led_49 (.in(and_49_out));
  and and_49 (and_49_out, not_7_out, in_9);
  and and_50 (and_50_out, not_7_out, in_10);
  LED led_50 (.in(and_50_out));
  LED led_51 (.in(and_51_out));
  and and_51 (and_51_out, not_7_out, in_11);
  LED led_52 (.in(and_52_out));
  and and_52 (and_52_out, not_7_out, in_12);
  LED led_53 (.in(and_53_out));
  and and_53 (and_53_out, not_7_out, in_13);
  and and_54 (and_54_out, not_7_out, in_14);
  LED led_54 (.in(and_54_out));
  and and_55 (and_55_out, not_7_out, in_15);
  LED led_55 (.in(and_55_out));
  and and_56 (and_56_out, not_7_out, in_16);
  LED led_56 (.in(and_56_out));
  and and_57 (and_57_out, not_8_out, in_9);
  LED led_57 (.in(and_57_out));
  and and_58 (and_58_out, not_8_out, in_10);
  LED led_58 (.in(and_58_out));
  LED led_59 (.in(and_59_out));
  and and_59 (and_59_out, not_8_out, in_11);
  LED led_60 (.in(and_60_out));
  and and_60 (and_60_out, not_8_out, in_12);
  LED led_61 (.in(and_61_out));
  and and_61 (and_61_out, not_8_out, in_13);
  LED led_62 (.in(and_62_out));
  and and_62 (and_62_out, not_8_out, in_14);
  LED led_63 (.in(and_63_out));
  and and_63 (and_63_out, not_8_out, in_15);
  LED led_64 (.in(and_64_out));
  and and_64 (and_64_out, not_8_out, in_16);

  // Notes on the sheet:
  //   8x8 Square LED Matrix simulation
  //   Drive (1 enables)
endmodule

module alternate (
);

  wire and_1_out, clock_1_out, demultiplexer_2_out0, demultiplexer_2_out1, demultiplexer_2_out2,
       demultiplexer_2_out3;
  wire [1:0] counter_2_q;
  wire [2:0] counter_1_q, demultiplexer_1_out0, demultiplexer_1_out1, demultiplexer_1_out2,
       demultiplexer_1_out3;
  wire [4:0] Memory_pointer_q;
  wire [7:0] not_1_out, ram_1_data;

  Counter #(.width(3), .max('h7)) counter_1 (.Q(counter_1_q), .clk(and_1_out));  // open: load, D, count, carry, clr
  Counter #(.width(5), .max('h1f)) Memory_pointer (
    .Q(Memory_pointer_q), .clk(clock_1_out));  // open: load, D, count, carry, clr
  Clock clock_1 (.out(clock_1_out));
  RAM #(.addrWidth(5), .bus("asynch")) ram_1 (.addr(Memory_pointer_q), .data(ram_1_data));  // open: sel, ld, clr
  Counter #(.width(2), .max('h3)) counter_2 (.Q(counter_2_q), .clk(clock_1_out));  // open: load, D, count, carry, clr
  and and_1 (and_1_out, counter_2_q[0], counter_2_q[1]);
  assign not_1_out = ~ram_1_data;  // NOT_Gate not_1, 8 bits wide
  _8x8_LED_Matrix_fan u_8x8_led_matrix_fan_1 (
    .Column(not_1_out), .Row_Address(demultiplexer_1_out0), .Enable(demultiplexer_2_out0));
  _8x8_LED_Matrix_fan u_8x8_led_matrix_fan_2 (
    .Column(not_1_out), .Row_Address(demultiplexer_1_out2), .Enable(demultiplexer_2_out2));
  _8x8_LED_Matrix_fan u_8x8_led_matrix_fan_3 (
    .Column(not_1_out), .Row_Address(demultiplexer_1_out1), .Enable(demultiplexer_2_out1));
  Demultiplexer #(.select(2), .width(3)) demultiplexer_1 (
    .out0(demultiplexer_1_out0), .out1(demultiplexer_1_out1), .out2(demultiplexer_1_out2),
    .out3(demultiplexer_1_out3), .in(counter_1_q), .sel(counter_2_q));  // open: en
  _8x8_LED_Matrix_fan u_8x8_led_matrix_fan_4 (
    .Column(not_1_out), .Row_Address(demultiplexer_1_out3), .Enable(demultiplexer_2_out3));
  Demultiplexer #(.select(2)) demultiplexer_2 (
    .out0(demultiplexer_2_out0), .out1(demultiplexer_2_out1), .out2(demultiplexer_2_out2),
    .out3(demultiplexer_2_out3), .in(1'b1), .sel(counter_2_q));  // open: en

  // Notes on the sheet:
  //   Row pointer
  //   Memory pointer
  //   Clock source (4 * 8 * 50hz =1.6Khz)
  //   Parallel EEPROM memory
  //   Active LED matrix pointer
  //   End of bank increment trigger
  //   LED matrix bank (should display the string "XCJ!")
  //   LED matrix row enabler
endmodule

module _8x8_LED_Matrix_fan (
  input  [7:0] Column,
  input  Enable,
  input  [2:0] Row_Address
);

  wire demultiplexer_1_out0, demultiplexer_1_out1, demultiplexer_1_out2, demultiplexer_1_out3,
       demultiplexer_1_out4, demultiplexer_1_out5, demultiplexer_1_out6, demultiplexer_1_out7;

  _8x8_LED_Matrix u_8x8_led_matrix_1 (
    .in_1(Column[7]), .in_2(Column[6]), .in_3(Column[5]), .in_4(Column[4]), .in_5(Column[3]),
    .in_6(Column[2]), .in_7(Column[1]), .Sink__0_enables(Column[0]), .in_9(demultiplexer_1_out0),
    .in_10(demultiplexer_1_out1), .in_11(demultiplexer_1_out2), .in_12(demultiplexer_1_out3),
    .in_13(demultiplexer_1_out4), .in_14(demultiplexer_1_out5), .in_15(demultiplexer_1_out6),
    .in_16(demultiplexer_1_out7));
  Demultiplexer #(.select(3)) demultiplexer_1 (
    .out0(demultiplexer_1_out0), .out1(demultiplexer_1_out1), .out2(demultiplexer_1_out2),
    .out3(demultiplexer_1_out3), .out4(demultiplexer_1_out4), .out5(demultiplexer_1_out5),
    .out6(demultiplexer_1_out6), .out7(demultiplexer_1_out7), .in(1'b1), .sel(Row_Address), .en(Enable));

  // Notes on the sheet:
  //   Convenience logic block to wrap LED Matrix
endmodule
